# Fritzing sketch Diagram_source (saved by Fritzing 0.9.5d)
breadboards: 1

parts:
  Part1 = Arduino Uno (Rev3) - ICSP
  Part2 = Adafruit PCA9685 PWM/Servo Breakout [part_number=815]
  J1 = Basic Servo
  J2 = Basic Servo
  J3 = Basic Servo
  J4 = Basic Servo
  J5 = Basic Servo
  Part3 = Thumb Joystick
  Part4 = Thumb Joystick
  R1 = Resistor [tolerance=±5% resistance=220 package="0402 [SMD]"]
  R2 = Resistor [tolerance=±5% resistance=220 package="0402 [SMD]"]

nets:
  N1: Part1.A0, Part4.VERT
  N2: Part1.A1, Part4.HORZ
  N3: Part1.A2, Part3.VERT
  N4: Part1.A3, Part3.HORZ
  N5: Part1.A4/SDA, Part2.SDA
  N6: Part1.A5/SCL, Part2.SCL
  N7: Part1.ICSP_MISO, Part1.D12/MISO, R2.Pin_0
  GND: Part1.GND, Part2.GND, J1.gnd, J2.gnd, J3.gnd, J4.gnd, J5.gnd, Part3.GND, Part4.GND
  N8: Part1.D13/SCK, R1.Pin_0
  VCC: Part1.5V, Part2.PWRIN, Part2.5.0V, Part2.VCC, J1.vcc, J2.vcc, J3.vcc, J4.vcc, J5.vcc, Part3.VCC, Part4.VCC
  N9: Part2.PWM4, J5.pulse
  N10: Part2.PWM3, J4.pulse
  N11: Part2.PWM2, J3.pulse
  N12: Part2.PWM1, J2.pulse
  N13: Part2.PWM0, J1.pulse
  N14: Part3.SEL, R1.Pin_1
  N15: Part4.SEL, R2.Pin_1

notes:
  5V4A +
  GND
  0 - Base Rotation
  1 - Shoulder
  2 - Elbow
  3 - Elbow
  4 - Gripper
  Left
  Joystick
  Right
  Joystick

custom parts:
  Adafruit PCA9685 PWM/Servo Breakout: Using only two pins, control 16 free-running PWM outputs! I2C-controlled PWM driver with a built in clock. Unlike the TLC5940 family, you do not need to continuously send it signal tying up your microcontroller, its completely free running! 5V compliant, which means you can control it from a 3.3V microcontroller and still safely drive up to 6V outputs (this is good for when you want to control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
